// Logisim project Final project.circ as structural Verilog: 7 circuits, main circuit main
module main (
  input  in_1,
  input  in_2,
  input  Register_destination,
  input  ALU_source,
  input  Memory_write,
  input  Memory_read,
  input  in_7,
  input  Memory_to_register,
  output out_9
);

  wire clock_1_out;
  wire [1:0] multiplexer_1_out;
  wire [2:0] adder_1_out, register_1_q;
  wire [3:0] rom_1_data_2;
  wire [9:0] bit_extender_1_out, multiplexer_2_out, multiplexer_3_out, n10_bit_alu_1_output,
       n10_bit_register_file_1_read_data_01, n10_bit_register_file_1_read_data_02, ram_1_data;
  wire [15:0] rom_1_data;

  Adder #(.width(3)) adder_1 (.a(register_1_q), .b(3'b001), .out(adder_1_out), .cin(in_1));  // open: cout
  Register #(.width(3)) register_1 (.D(adder_1_out), .Q(register_1_q), .clk(clock_1_out));  // open: en, clr
  Main_control main_control_1 (.in_1(rom_1_data_2), .out_2(rom_1_data[3:2]));
  ROM #(.addrWidth(3), .dataWidth(16)) rom_1 (
    .addr(register_1_q), .data({rom_1_data[15:10], rom_1_data_2, rom_1_data[5:0]}));  // open: sel
  Multiplexer #(.width(2)) multiplexer_1 (
    .in0(rom_1_data[3:2]), .in1(rom_1_data[1:0]), .out(multiplexer_1_out), .sel(Register_destination));  // open: en
  Multiplexer #(.width(10)) multiplexer_2 (
    .in0(n10_bit_alu_1_output), .in1(ram_1_data), .out(multiplexer_2_out), .sel(Memory_to_register));  // open: en
  _10_bit_register_file u_10_bit_register_file_1 (
    .Write_data(multiplexer_2_out), .Write_register(multiplexer_1_out), .Read_register_01(rom_1_data[5:4]),
    .Read_data_01(n10_bit_register_file_1_read_data_01), .Read_data_02(n10_bit_register_file_1_read_data_02),
    .Read_register_02(rom_1_data[3:2]), .Write_control_signal(in_7), .Clock(clock_1_out));
  Clock clock_1 (.out(clock_1_out));
  Multiplexer #(.width(10)) multiplexer_3 (
    .in0(n10_bit_register_file_1_read_data_02), .in1(bit_extender_1_out), .out(multiplexer_3_out),
    .sel(ALU_source));  // open: en
  assign bit_extender_1_out = {{8{1'b0}}, rom_1_data[1:0]};  // Bit_Extender bit_extender_1
  _10_bit_ALU u_10_bit_alu_1 (
    .Carry_Out(out_9), .Operation(rom_1_data_2), .Carry_In(in_2), .A(n10_bit_register_file_1_read_data_01),
    .B(multiplexer_3_out), .Output(n10_bit_alu_1_output));
  RAM #(.addrWidth(10), .dataWidth(10), .bus("separate")) ram_1 (
    .addr(n10_bit_alu_1_output), .din(n10_bit_register_file_1_read_data_02), .data(ram_1_data),
    .str(Memory_write), .clk(clock_1_out), .ld(Memory_read));  // open: sel, clr

  // Notes on the sheet:
  //   contents of rom_1 (hex, n*v repeats v):
  //   2012
endmodule

module _10_bit_register_file (
  input  [9:0] Write_data,
  input  [1:0] Read_register_01,
  input  [1:0] Read_register_02,
  input  [1:0] Write_register,
  input  Write_control_signal,
  input  Clock,
  output [9:0] Read_data_01,
  output [9:0] Read_data_02
);

  wire and_1_out, decoder_1_out0, decoder_1_out1, decoder_1_out2, decoder_1_out3;
  wire [9:0] register_1_q, register_2_q, register_3_q, register_4_q;

  Decoder #(.select(2)) decoder_1 (
    .out0(decoder_1_out0), .out1(decoder_1_out1), .out2(decoder_1_out2), .out3(decoder_1_out3),
    .sel(Write_register));  // open: en
  Register #(.width(10)) register_1 (
    .D(Write_data), .en(decoder_1_out0), .Q(register_1_q), .clk(and_1_out));  // open: clr
  Register #(.width(10)) register_2 (
    .D(Write_data), .en(decoder_1_out1), .Q(register_2_q), .clk(and_1_out));  // open: clr
  Register #(.width(10)) register_3 (
    .D(Write_data), .en(decoder_1_out2), .Q(register_3_q), .clk(and_1_out));  // open: clr
  Register #(.width(10)) register_4 (
    .D(Write_data), .en(decoder_1_out3), .Q(register_4_q), .clk(and_1_out));  // open: clr
  and and_1 (and_1_out, Write_control_signal, Clock);
  Multiplexer #(.select(2), .width(10)) multiplexer_1 (
    .in0(register_1_q), .in1(register_2_q), .in2(register_3_q), .in3(register_4_q), .out(Read_data_01),
    .sel(Read_register_01));  // open: en
  Multiplexer #(.select(2), .width(10)) multiplexer_2 (
    .in0(register_1_q), .in1(register_2_q), .in2(register_3_q), .in3(register_4_q), .out(Read_data_02),
    .sel(Read_register_02));  // open: en
endmodule

module _1_bit_ALU (
  input  Carry_In,
  input  A,
  input  A_2,
  input  [3:0] SELECT_BITS,
  output Output,
  output Carry_Out
);

  wire adder_1_cout, adder_1_out, and_1_out, or_1_out, subtractor_1_bout, subtractor_1_out;

  and and_1 (and_1_out, A, A_2);
  or or_1 (or_1_out, A, A_2);
  Adder #(.width(1)) adder_1 (.a(A), .b(A_2), .out(adder_1_out), .cin(Carry_In), .cout(adder_1_cout));
  Subtractor #(.width(1)) subtractor_1 (
    .a(A), .b(A_2), .out(subtractor_1_out), .bin(Carry_In), .bout(subtractor_1_bout));
  Multiplexer #(.select(4)) multiplexer_1 (
    .in0(and_1_out), .in1(or_1_out), .in2(adder_1_out), .in3(subtractor_1_out), .out(Output),
    .sel(SELECT_BITS));  // open: in4, in5, in6, in7, in8, in9, in10, in11, in12, in13, in14, in15, en
  Multiplexer #(.select(4)) multiplexer_2 (
    .in0(adder_1_cout), .in1(subtractor_1_bout), .out(Carry_Out), .sel(SELECT_BITS));  // open: in2, in3, in4, in5, in6, in7, in8, in9, in10, in11, in12, in13, in14, in15, en
endmodule

module _10_bit_ALU (
  input  Carry_In,
  input  [3:0] Operation,
  input  [9:0] A,
  input  [9:0] B,
  output [9:0] Output,
  output Carry_Out
);

  wire n1_bit_alu_1_carry_out, n1_bit_alu_2_carry_out, n1_bit_alu_3_carry_out, n1_bit_alu_4_carry_out,
       n1_bit_alu_5_carry_out, n1_bit_alu_6_carry_out, n1_bit_alu_7_carry_out, n1_bit_alu_8_carry_out,
       n1_bit_alu_9_carry_out;

  _1_bit_ALU u_1_bit_alu_1 (
    .A(A[0]), .A_2(B[0]), .Output(Output[0]), .Carry_Out(n1_bit_alu_1_carry_out), .Carry_In(Carry_In),
    .SELECT_BITS(Operation));
  _1_bit_ALU u_1_bit_alu_2 (
    .A(A[1]), .A_2(B[1]), .Output(Output[1]), .Carry_Out(n1_bit_alu_2_carry_out),
    .Carry_In(n1_bit_alu_1_carry_out), .SELECT_BITS(Operation));
  _1_bit_ALU u_1_bit_alu_3 (
    .A(A[2]), .A_2(B[2]), .Output(Output[2]), .Carry_Out(n1_bit_alu_3_carry_out),
    .Carry_In(n1_bit_alu_2_carry_out), .SELECT_BITS(Operation));
  _1_bit_ALU u_1_bit_alu_4 (
    .A(A[3]), .A_2(B[3]), .Output(Output[3]), .Carry_Out(n1_bit_alu_4_carry_out),
    .Carry_In(n1_bit_alu_3_carry_out), .SELECT_BITS(Operation));
  _1_bit_ALU u_1_bit_alu_5 (
    .A(A[4]), .A_2(B[4]), .Output(Output[4]), .Carry_Out(n1_bit_alu_5_carry_out),
    .Carry_In(n1_bit_alu_4_carry_out), .SELECT_BITS(Operation));
  _1_bit_ALU u_1_bit_alu_6 (
    .A(A[5]), .A_2(B[5]), .Output(Output[5]), .Carry_Out(n1_bit_alu_6_carry_out),
    .Carry_In(n1_bit_alu_5_carry_out), .SELECT_BITS(Operation));
  _1_bit_ALU u_1_bit_alu_7 (
    .A(A[6]), .A_2(B[6]), .Output(Output[6]), .Carry_Out(n1_bit_alu_7_carry_out),
    .Carry_In(n1_bit_alu_6_carry_out), .SELECT_BITS(Operation));
  _1_bit_ALU u_1_bit_alu_8 (
    .A(A[7]), .A_2(B[7]), .Output(Output[7]), .Carry_Out(n1_bit_alu_8_carry_out),
    .Carry_In(n1_bit_alu_7_carry_out), .SELECT_BITS(Operation));
  _1_bit_ALU u_1_bit_alu_9 (
    .A(A[8]), .A_2(B[8]), .Output(Output[8]), .Carry_Out(n1_bit_alu_9_carry_out),
    .Carry_In(n1_bit_alu_8_carry_out), .SELECT_BITS(Operation));
  _1_bit_ALU u_1_bit_alu_10 (
    .A(A[9]), .A_2(B[9]), .Output(Output[9]), .Carry_Out(Carry_Out), .Carry_In(n1_bit_alu_9_carry_out),
    .SELECT_BITS(Operation));
endmodule

module Single_cycle_datapath_for_R_type_instructions (
  input  in_1,
  input  in_2,
  input  in_3,
  output [9:0] out_4,
  output out_5
);

  wire clock_1_out;
  wire [2:0] adder_1_out, register_1_q;
  wire [9:0] n10_bit_register_file_1_read_data_01, n10_bit_register_file_1_read_data_02;
  wire [15:0] rom_1_data;

  Adder #(.width(3)) adder_1 (.a(register_1_q), .b(3'b001), .out(adder_1_out), .cin(in_1));  // open: cout
  Register #(.width(3)) register_1 (.D(adder_1_out), .Q(register_1_q), .clk(clock_1_out));  // open: en, clr
  ROM #(.addrWidth(3), .dataWidth(16)) rom_1 (.addr(register_1_q), .data(rom_1_data));  // open: sel
  _10_bit_register_file u_10_bit_register_file_1 (
    .Write_data(out_4), .Write_register(rom_1_data[1:0]), .Read_register_01(rom_1_data[5:4]),
    .Read_data_01(n10_bit_register_file_1_read_data_01), .Read_data_02(n10_bit_register_file_1_read_data_02),
    .Read_register_02(rom_1_data[3:2]), .Write_control_signal(in_3), .Clock(clock_1_out));
  Clock clock_1 (.out(clock_1_out));
  _10_bit_ALU u_10_bit_alu_1 (
    .Carry_Out(out_5), .Operation(rom_1_data[9:6]), .Carry_In(in_2),
    .A(n10_bit_register_file_1_read_data_01), .B(n10_bit_register_file_1_read_data_02), .Output(out_4));

  // Notes on the sheet:
  //   contents of rom_1 (hex, n*v repeats v):
  //   1014 235 3456
endmodule

module Single_cycle_datapath_for_I_type_instructions (
  input  in_1,
  input  in_2,
  input  in_3,
  input  in_4,
  input  in_5,
  output out_6
);

  wire clock_1_out;
  wire [2:0] adder_1_out, register_1_q;
  wire [9:0] bit_extender_1_out, n10_bit_alu_1_output, n10_bit_register_file_1_read_data_01,
       n10_bit_register_file_1_read_data_02, ram_1_data;
  wire [15:0] rom_1_data;

  Adder #(.width(3)) adder_1 (.a(register_1_q), .b(3'b001), .out(adder_1_out), .cin(in_2));  // open: cout
  ROM #(.addrWidth(3), .dataWidth(16)) rom_1 (.addr(register_1_q), .data(rom_1_data));  // open: sel
  Register #(.width(3)) register_1 (.D(adder_1_out), .Q(register_1_q), .clk(clock_1_out));  // open: en, clr
  _10_bit_register_file u_10_bit_register_file_1 (
    .Write_data(ram_1_data), .Write_register(rom_1_data[3:2]), .Read_register_01(rom_1_data[5:4]),
    .Read_data_01(n10_bit_register_file_1_read_data_01), .Read_data_02(n10_bit_register_file_1_read_data_02),
    .Read_register_02(rom_1_data[3:2]), .Write_control_signal(in_5), .Clock(clock_1_out));
  Clock clock_1 (.out(clock_1_out));
  assign bit_extender_1_out = {{8{1'b0}}, rom_1_data[1:0]};  // Bit_Extender bit_extender_1
  _10_bit_ALU u_10_bit_alu_1 (
    .Carry_Out(out_6), .Operation(rom_1_data[9:6]), .Carry_In(in_1),
    .A(n10_bit_register_file_1_read_data_01), .B(bit_extender_1_out), .Output(n10_bit_alu_1_output));
  RAM #(.addrWidth(10), .dataWidth(10), .bus("separate")) ram_1 (
    .addr(n10_bit_alu_1_output), .din(n10_bit_register_file_1_read_data_02), .data(ram_1_data), .str(in_3),
    .clk(clock_1_out), .ld(in_4));  // open: sel, clr

  // Notes on the sheet:
  //   contents of rom_1 (hex, n*v repeats v):
  //   6146 a243
endmodule

module Main_control (
  input  [3:0] in_1,
  output [1:0] out_2
);

  wire decoder_1_out1, decoder_1_out3, decoder_1_out4, decoder_1_out5, decoder_1_out6;

  Decoder #(.select(4)) decoder_1 (
    .out1(decoder_1_out1), .out3(decoder_1_out3), .out4(decoder_1_out4), .out5(decoder_1_out5),
    .out6(decoder_1_out6), .sel(in_1));  // open: out0, out2, out7, out8, out9, out10, out11, out12, out13, out14, out15, en
  or or_1 (out_2[0], decoder_1_out1, decoder_1_out4, decoder_1_out6);
  or or_2 (out_2[1], decoder_1_out3, decoder_1_out4, decoder_1_out5, decoder_1_out6);
endmodule
